# Fritzing sketch wm-refill-dispenser (saved by Fritzing 0.9.3b)
circuit board: 8.46667cm x 5.64444cm
breadboards: 1

parts:
  Bauteil1 = Arduino Mega 2560 (Rev3)
  J1 = female pin header, 2 pins [form="♀ (female)"]
  R1 = Resistor [tolerance=±5% resistance=10k package=THT]
  C1 = Electrolytic Capacitor [capacitance=22µF package="100 mil [THT, electrolytic]"]
  R2 = Resistor [tolerance=±5% resistance=10k package=THT]
  R3 = Resistor [tolerance=±5% resistance=10k package=THT]
  VCC1 = Battery block 9V
  C2 = Electrolytic Capacitor [capacitance=22µF package="100 mil [THT, electrolytic]"]
  R5 = Resistor [tolerance=±5% resistance=10k package=THT]
  R6 = Resistor [tolerance=±5% resistance=10k package=THT]
  R4 = Resistor [tolerance=±5% resistance=10k package=THT]
  U1 = LM 358 Dual Op-Amp [package="DIP8 [THT]"]
  R7 = Resistor [tolerance=±5% resistance=10k package=THT]
  S1 = Pushbutton [package="[THT]"]
  hc-sr1 = hc-sr04
  ZS-042_RTC1 = ZS-042 RTC Module
  Bauteil2 = IFR520 MOS module [package=THT]
  Bauteil3 = IFR520 MOS module [package=THT]
  U2 = RJ45 Jack [package=rj45-8]
  U3 = RJ45 Jack [package=rj45-8]
  R8 = Resistor [tolerance=±5% resistance=15k package=THT]
  R9 = Resistor [tolerance=±5% resistance=1k package=THT]
  R10 = Resistor [tolerance=±5% resistance=2.2k package=THT]
  U6 = ESP8266 WiFi Module [part_number=ESP8266]
  J2 = Piezo Speaker

nets (from the schematic view):
  N1: Bauteil1.D21/SCL, Bauteil1.SCL, ZS-042_RTC1.SCL
  N2: Bauteil1.D20/SDA, Bauteil1.SDA, ZS-042_RTC1.SDA
  GND: Bauteil1.GND, C1.-, R2.Pin_0, VCC1.-, C2.-, R5.Pin_0, U1.connector3, R7.Pin_1, hc-sr1.GND, ZS-042_RTC1.GND, Bauteil2.GND, Bauteil3.GND, U2.8, U3.8, R8.Pin_0, R10.Pin_0, U6.GND, J2.pin1
  3V3: Bauteil1.3V3, U6.VCC, U6.CH_PD, U6.REST
  VIN: Bauteil1.VIN, VCC1.+, U1.connector7, Bauteil2.VIN, Bauteil3.VIN
  N3: Bauteil1.D0_RX0, U6.TXD
  N4: Bauteil1.D1_TX0, R9.Pin_0
  N5: Bauteil1.D2_PWM, R4.Pin_0
  N6: Bauteil1.D3_PWM, R1.Pin_0
  N7: Bauteil1.D4_PWM, Bauteil3.SIG
  N8: Bauteil1.D5_PWM, Bauteil2.SIG
  5V Arduino: Bauteil1.5V, S1.Pin_1, S1.Pin_2, hc-sr1.VCC, ZS-042_RTC1.VCC, Bauteil2.VCC, Bauteil3.VCC, U2.7, U3.6, U3.7
  N9: Bauteil1.D22, R7.Pin_0, S1.Pin_3, S1.Pin_4
  N10: Bauteil1.D24, U2.1
  N11: Bauteil1.D26, U2.6, R8.Pin_1
  N12: Bauteil1.D28, U2.2
  N13: Bauteil1.D30, J2.pin2
  N14: J1.pin1, R3.Pin_1, U1.connector0
  N15: J1.pin2, R6.Pin_1, U1.connector6
  N16: R1.Pin_1, C1.+, U1.connector2
  N17: R2.Pin_1, R3.Pin_0, U1.connector1
  N18: C2.+, R4.Pin_1, U1.connector4
  N19: R5.Pin_1, R6.Pin_0, U1.connector5
  N20: hc-sr1.Trig, U3.2
  N21: hc-sr1.Echo, U3.1
  N22: R9.Pin_1, R10.Pin_1, U6.RXD

notes:
  Option - Food Break Switch

// code stored in the sketch: complex-v1.ino
/*
  Fade

  This example shows how to fade an LED on pin 9 using the analogWrite()
  function.

  The analogWrite() function uses PWM, so if you want to change the pin you're
  using, be sure to use another PWM capable pin. On most Arduino, the PWM pins
  are identified with a "~" sign, like ~3, ~5, ~6, ~9, ~10 and ~11.

  This example code is in the public domain.

  http://www.arduino.cc/en/Tutorial/Fade
*/

int pump1 = 3;           // the PWM pin the controller is attached to
int pump1Min = 10;
int pump1Max = 200;
int pump1Current = 0;
int brightness = 10;    // how bright the LED is
int fadeAmount = 5;    // how many points to fade the LED by
int t1 = 1; // time in secs. to stay at level min
int t2 = 2; // time in secs. to stay at max
int t3 = 1; // time in secs. to go from min to max
int t4 = 1; // time in secs. to go from max to min
char step = 't1'; // step marker

// the setup routine runs once when you press reset:
void setup() {
  // declare pin 9 to be an output:
  pinMode(pump1, pump1Current);
}



// the loop routine runs over and over again forever:
void loop() {
  pump1();
  //pumpOn();
  //delay(300);
  //pumpOff();
  //delay(500);
}

void pump1() {
  
}
void pumpOn() {
  // set the brightness of pin 9:
  analogWrite(pump1, brightness);

  // change the brightness for next time through the loop:
  brightness = brightness + fadeAmount;

  // reverse the direction of the fading at the ends of the fade:
  if (brightness <= 0 || brightness >= 255) {
    fadeAmount = -fadeAmount;
  }
  // wait for 30 milliseconds to see the dimming effect
  delay(10);
}
void pumpOff() {
  // set the brightness of pin 9:
  analogWrite(pump1, brightness);

  // change the brightness for next time through the loop:
  brightness = brightness - fadeAmount;

  // reverse the direction of the fading at the ends of the fade:
  if (brightness <= 0 || brightness >= 255) {
    fadeAmount = -fadeAmount;
  }
  // wait for 30 milliseconds to see the dimming effect
  delay(30);
}
